# Fritzing sketch home-made-google-home (saved by Fritzing 0.9.3b)

parts:
  Raspberry_Pi_1 = Raspberry Pi 3 [part_number=RPI-3-V1.2]
  LED1 = smd LED [color="Red (633nm)" package="0805 [SMD]"]

nets:
  N1: Raspberry_Pi_1.GIPO25, LED1.anode
  N2: Raspberry_Pi_1.GND, LED1.cathode
